// Logisim project CPU_t3.circ as structural Verilog: 5 circuits, main circuit main
module main (
  input  [31:0] in_1,
  input  [31:0] in_2,
  output [31:0] out_3,
  output [19:0] out_4
);

  wire and_1_out, and_2_out, and_3_out, buzzer_1_p3, CLK, cpu_1_read, cpu_1_write, decoder_1_out0,
       keyboard_1_avail, not_1_out, por_1_out, rgb_video_1_p2, undriven_2, undriven_3;
  wire [6:0] keyboard_1_data;
  wire [19:0] bitselector_1_out;
  wire [23:0] buzzer_1_p1;
  wire [31:0] controlled_buffer_1_out, cpu_1_outaddress, cpu_1_outdata, IR, MDR, PC, ram_1_dout, ram_2_dout,
       undriven;

  Hex_Digit_Display hex_digit_display_1 (.value(PC[31:28]));  // open: dp
  Hex_Digit_Display hex_digit_display_2 (.value(PC[27:24]));  // open: dp
  Hex_Digit_Display hex_digit_display_3 (.value(MDR[31:28]));  // open: dp
  Hex_Digit_Display hex_digit_display_4 (.value(MDR[27:24]));  // open: dp
  Hex_Digit_Display hex_digit_display_5 (.value(IR[31:28]));  // open: dp
  Hex_Digit_Display hex_digit_display_6 (.value(IR[27:24]));  // open: dp
  Hex_Digit_Display hex_digit_display_7 (.value(PC[23:20]));  // open: dp
  Hex_Digit_Display hex_digit_display_8 (.value(PC[19:16]));  // open: dp
  Hex_Digit_Display hex_digit_display_9 (.value(MDR[23:20]));  // open: dp
  Hex_Digit_Display hex_digit_display_10 (.value(MDR[19:16]));  // open: dp
  Hex_Digit_Display hex_digit_display_11 (.value(IR[23:20]));  // open: dp
  Hex_Digit_Display hex_digit_display_12 (.value(IR[19:16]));  // open: dp
  Clock clock_1 (.out(CLK));
  Hex_Digit_Display hex_digit_display_13 (.value(PC[15:12]));  // open: dp
  Hex_Digit_Display hex_digit_display_14 (.value(PC[11:8]));  // open: dp
  Hex_Digit_Display hex_digit_display_15 (.value(MDR[15:12]));  // open: dp
  Hex_Digit_Display hex_digit_display_16 (.value(MDR[11:8]));  // open: dp
  Hex_Digit_Display hex_digit_display_17 (.value(IR[15:12]));  // open: dp
  Hex_Digit_Display hex_digit_display_18 (.value(IR[11:8]));  // open: dp
  CPU cpu_1 (
    .CLK(CLK), .inData(out_3), .inAddress(undriven), .outAddress(cpu_1_outaddress), .outData(cpu_1_outdata),
    .Read(cpu_1_read), .Write(cpu_1_write), .deb_PC(PC), .deb_IR(IR), .deb_MDR(MDR));  // open: in_4, in_5, in_6, in_7, in_8, in_9, in_10, in_11, in_12, in_13, debAdrReg, debSP, debFlagReg
  Hex_Digit_Display hex_digit_display_19 (.value(PC[7:4]));  // open: dp
  Hex_Digit_Display hex_digit_display_20 (.value(PC[3:0]));  // open: dp
  Hex_Digit_Display hex_digit_display_21 (.value(MDR[7:4]));  // open: dp
  Hex_Digit_Display hex_digit_display_22 (.value(MDR[3:0]));  // open: dp
  Hex_Digit_Display hex_digit_display_23 (.value(IR[7:4]));  // open: dp
  Hex_Digit_Display hex_digit_display_24 (.value(IR[3:0]));  // open: dp
  Hex_Digit_Display hex_digit_display_25 (.value(in_2[31:28]));  // open: dp
  BitSelector #(.group(20), .width(32)) bitselector_1 (.in(cpu_1_outaddress), .out(bitselector_1_out), .sel(1'b0));
  Hex_Digit_Display hex_digit_display_26 (.value(in_2[27:24]));  // open: dp
  Hex_Digit_Display hex_digit_display_27 (.value(in_2[23:20]));  // open: dp
  Decoder #(.select(4)) decoder_1 (
    .out0(decoder_1_out0), .sel(cpu_1_outaddress[31:28]));  // open: out1, out2, out3, out4, out5, out6, out7, out8, out9, out10, out11, out12, out13, out14, out15, en
  Hex_Digit_Display hex_digit_display_28 (.value(in_2[19:16]));  // open: dp
  Hex_Digit_Display hex_digit_display_29 (.value(in_2[15:12]));  // open: dp
  and and_1 (and_1_out, decoder_1_out0, cpu_1_write);
  Hex_Digit_Display hex_digit_display_30 (.value(in_2[11:8]));  // open: dp
  Hex_Digit_Display hex_digit_display_31 (.value(in_2[7:4]));  // open: dp
  Keyboard keyboard_1 (.clk(CLK), .re(buzzer_1_p3), .clr(undriven_2), .avail(keyboard_1_avail), .data(keyboard_1_data));
  Decoder #(.select(3)) decoder_2 ();  // open: out0, out1, out2, out3, out4, out5, out6, out7, sel, en
  POR por_1 (.out(por_1_out));
  and and_2 (and_2_out, CLK, ~por_1_out);  // AND_Gate
  RAM #(.addrWidth(20), .dataWidth(32), .trigger("falling"), .\type ("nonvolatile")) ram_1 (
    .addr(bitselector_1_out), .we(cpu_1_write), .oe(cpu_1_read), .clk(and_2_out),
    .din(controlled_buffer_1_out), .dout(ram_1_dout));
  assign controlled_buffer_1_out = and_1_out ? cpu_1_outdata : 32'bz;  // Controlled_Buffer controlled_buffer_1
  BitSelector #(.group(20), .width(32)) bitselector_2 (.in(in_1), .out(out_4), .sel(1'b0));
  Hex_Digit_Display hex_digit_display_32 (.value(in_2[3:0]));  // open: dp
  and and_3 (and_3_out, decoder_1_out0, cpu_1_read);
  assign out_3 = and_3_out ? ram_1_dout : 32'bz;  // Controlled_Buffer controlled_buffer_2
  // Buzzer buzzer_1: pin names not known; wires that end beside it: buzzer_1_p1, keyboard_1_data, buzzer_1_p3, keyboard_1_data
  not not_1 (not_1_out, undriven_3);
  TTY #(.cols(64), .rows(32)) tty_1 ();  // open: data, clk, we, clr
  RAM #(.addrWidth(16), .dataWidth(32)) ram_2 (
    .addr(buzzer_1_p1[15:0]), .we(undriven_3), .oe(not_1_out), .clk(CLK), .din(ram_2_dout), .dout(ram_2_dout));
  ROM #(.addrWidth(24)) rom_1 (.addr(buzzer_1_p1), .data(ram_2_dout[7:0]));
  // RGB_Video rgb_video_1: pin names not known; wires that end beside it: CLK, rgb_video_1_p2, rgb_video_1_p2, buzzer_1_p3, keyboard_1_data, keyboard_1_data, keyboard_1_data
  // Pins of 16 and 24 bits meet at buzzer_1_p1
  // Pins of 8 and 32 bits meet at ram_2_dout
endmodule

module CPU (
  input  CLK,
  input  [31:0] inData,
  input  [31:0] inAddress,
  input  in_4,
  input  in_5,
  input  in_6,
  input  in_7,
  input  in_8,
  input  in_9,
  input  in_10,
  input  in_11,
  input  in_12,
  input  in_13,
  output [31:0] outAddress,
  output [31:0] outData,
  output Read,
  output Write,
  output [31:0] deb_PC,
  output [31:0] deb_IR,
  output debAdrReg,
  output debSP,
  output [31:0] deb_MDR,
  output debFlagReg
);

  wire ACC_we, ADR_out, ADR_we, ALU_in, and_1_out, CLK_t, comparator_1_eq, comparator_1_gt, comparator_1_lt,
       FR_cls, I3B, INT_we, Interrupt_q, IR_out, IR_we, MAR_load, MAR_we, MDR_out, MDR_we, or_1_out, PC_enb,
       PC_load, PC_mux, Posta_out, Posta_we, REG_out, REG_we, TEMP_out, TEMP_we, undriven, undriven_2,
       undriven_3, undriven_4;
  wire [2:0] REG_inSelect, REG_outSelect;
  wire [4:0] FlagRegister_q, undriven_5;
  wire [7:0] adder_1_out, controlled_buffer_1_out, controlled_buffer_2_out, controlled_buffer_5_out,
       demultiplexer_1_out0, demultiplexer_1_out1, multiplexer_1_out, StackReg_q, StackRegister_q,
       subtractor_1_out;
  wire [31:0] ACC_q, AddressRegister_q, alu_1_alu_out, controlled_buffer_3_out, controlled_buffer_4_out,
       controlled_buffer_7_out, multiplexer_2_out, multiplexer_3_out, registerfile_1_regout, TEMP_q;

  Clock clock_1 (.out(CLK_t));
  Register #(.width(32)) MDR (.D(inData), .en(MDR_we), .clk(CLK_t), .Q(deb_MDR));  // open: clr
  Register #(.width(32)) AddressRegister (.D(inAddress), .en(ADR_we), .clk(CLK_t), .Q(AddressRegister_q));  // open: clr
  Register #(.width(1)) Interrupt (.D(undriven), .en(INT_we), .clk(CLK_t), .Q(Interrupt_q));  // open: clr
  assign controlled_buffer_1_out = in_4 ? controlled_buffer_2_out : 8'bz;  // Controlled_Buffer controlled_buffer_1
  Demultiplexer #(.width(8)) demultiplexer_1 (
    .out0(demultiplexer_1_out0), .out1(demultiplexer_1_out1), .in(controlled_buffer_2_out), .sel(in_5));
  assign controlled_buffer_2_out = in_6 ? StackRegister_q : 8'bz;  // Controlled_Buffer controlled_buffer_2
  assign controlled_buffer_3_out = MDR_out ? deb_MDR : 32'bz;  // Controlled_Buffer controlled_buffer_3
  assign controlled_buffer_4_out = ADR_out ? AddressRegister_q : 32'bz;  // Controlled_Buffer controlled_buffer_4
  assign controlled_buffer_5_out = in_9 ? StackReg_q : 8'bz;  // Controlled_Buffer controlled_buffer_5
  RegisterFile registerfile_1 (
    .CLK(CLK_t), .inData(controlled_buffer_3_out), .WE(REG_we), .REG_inSel(REG_inSelect),
    .REG_outSel(REG_outSelect), .OUT_enb(REG_out), .regOut(registerfile_1_regout));
  Adder adder_1 (.a(demultiplexer_1_out0), .b(8'h1), .out(adder_1_out));  // open: cin, cout
  Subtractor subtractor_1 (.a(demultiplexer_1_out1), .b(8'h1), .out(subtractor_1_out));  // open: bin, bout
  assign controlled_buffer_3_out = 1'b0 ? registerfile_1_regout : 32'bz;  // Controlled_Buffer controlled_buffer_6
  Multiplexer #(.width(8)) multiplexer_1 (
    .in0(adder_1_out), .in1(subtractor_1_out), .out(multiplexer_1_out), .sel(in_5));
  Register #(.width(32)) TEMP (.D(registerfile_1_regout), .en(TEMP_we), .clk(CLK_t), .Q(TEMP_q));  // open: clr
  Register #(.width(32)) InstructionRegister (
    .D(controlled_buffer_3_out), .en(IR_we), .clk(CLK_t), .Q(deb_IR));  // open: clr
  Register StackRegister (.D(multiplexer_1_out), .en(in_7), .clk(in_8), .Q(StackRegister_q));  // open: clr
  Counter StackReg (.load(in_11), .count(in_12), .Q(StackReg_q), .up(in_10), .clk(in_13));  // open: D, carry, clr
  Multiplexer #(.width(32)) multiplexer_2 (
    .in0(registerfile_1_regout), .in1(controlled_buffer_3_out), .out(multiplexer_2_out), .sel(1'b0));
  ALU alu_1 (.inA(TEMP_q), .inB(multiplexer_2_out), .ALU_out(alu_1_alu_out));  // open: ShiftAmount
  ControlUnit controlunit_1 (
    .CLK(CLK_t), .IR_in(deb_IR),
    .controlBits({ALU_in, FR_cls, ACC_we, MAR_we, MAR_load, I3B, ADR_out, ADR_we, Posta_out, Posta_we, TEMP_out, TEMP_we, IR_out, IR_we, MDR_out, MDR_we, PC_load, PC_enb, PC_mux, Read}));
  assign controlled_buffer_7_out = 1'b0 ? controlled_buffer_4_out : 32'bz;  // Controlled_Buffer controlled_buffer_7
  and and_1 (and_1_out, undriven_2, or_1_out);
  or or_1 (or_1_out, undriven_3, undriven_4);
  Register #(.width(32)) ACC (.D(alu_1_alu_out), .en(ACC_we), .clk(CLK_t), .Q(ACC_q));  // open: clr
  Counter #(.max('hffffffff), .width(32)) ProgramCounter (
    .load(1'b0), .D(controlled_buffer_7_out), .count(PC_enb), .Q(deb_PC), .clk(CLK_t));  // open: carry, up, clr
  Multiplexer #(.width(32)) multiplexer_3 (
    .in0(deb_PC), .in1(controlled_buffer_4_out), .out(multiplexer_3_out), .sel(PC_mux));
  Comparator #(.width(32)) comparator_1 (
    .a(ACC_q), .gt(comparator_1_gt), .eq(comparator_1_eq), .lt(comparator_1_lt));  // open: b
  Register #(.width(32)) MAR (.D(multiplexer_3_out), .en(MAR_we), .clk(CLK_t), .Q(outAddress));  // open: clr
  Register #(.width(5)) FlagRegister (.D(undriven_5), .clk(CLK_t), .Q(FlagRegister_q));  // open: en, clr

  assign outData = {32{1'b0}};
  assign Write = 1'b0;

  // Other names for the same wires on the sheet: IR_data[31:0] = deb_IR; MDR_data[31:0] = deb_MDR

  // Notes on the sheet:
  //   I3B
  //   I3B
  //   carry
  //   Flagreg
  //   flagReg.m_carry
endmodule

module ALU (
  input  [31:0] inA,
  input  [31:0] inB,
  input  [4:0] ShiftAmount,
  output [31:0] ALU_out
);

  wire adder_1_cout, subtractor_1_bout, undriven, undriven_2;
  wire [31:0] adder_1_out, and_1_out, not_1_out, or_1_out, shifter_1_out, shifter_2_out, subtractor_1_out,
       xor_1_out;

  Adder #(.width(32)) adder_1 (.a(inA), .b(inB), .out(adder_1_out), .cin(undriven), .cout(adder_1_cout));
  Subtractor #(.width(32)) subtractor_1 (
    .a(inA), .b(inB), .out(subtractor_1_out), .bin(undriven_2), .bout(subtractor_1_bout));
  Multiplier #(.width(32)) multiplier_1 ();  // open: a, b, out, cin, cout
  Divider divider_1 ();  // open: a, b, out, upper, rem
  Comparator comparator_1 ();  // open: a, b, gt, eq, lt
  Shifter #(.width(32)) shifter_1 (.in(inA), .\dist (ShiftAmount), .out(shifter_1_out));
  Shifter #(.shift("lr"), .width(32)) shifter_2 (.in(inA), .\dist (ShiftAmount), .out(shifter_2_out));
  assign and_1_out = inA & inB;  // AND_Gate and_1, 32 bits wide
  assign not_1_out = ~inA;  // NOT_Gate not_1, 32 bits wide
  assign or_1_out = inA | inB;  // OR_Gate or_1, 32 bits wide
  assign xor_1_out = inA ^ inB;  // XOR_Gate xor_1, 32 bits wide
  Multiplexer #(.select(4), .width(32)) multiplexer_1 (.out(ALU_out));  // open: in0, in1, in2, in3, in4, in5, in6, in7, in8, in9, in10, in11, in12, in13, in14, in15, sel

  // Notes on the sheet:
  //   2s comp
endmodule

module RegisterFile (
  input  CLK,
  input  [31:0] inData,
  input  WE,
  input  [2:0] REG_inSel,
  input  [2:0] REG_outSel,
  input  OUT_enb,
  output [31:0] regOut
);

  wire demultiplexer_1_out0, demultiplexer_1_out1, demultiplexer_1_out2, demultiplexer_1_out3,
       demultiplexer_1_out4, demultiplexer_1_out5, demultiplexer_1_out6, demultiplexer_1_out7;
  wire [31:0] reg0_q, reg1_q, reg2_q, reg3_q, reg4_q, reg5_q, reg6_q, reg7_q;

  Demultiplexer #(.select(3)) demultiplexer_1 (
    .out0(demultiplexer_1_out0), .out1(demultiplexer_1_out1), .out2(demultiplexer_1_out2),
    .out3(demultiplexer_1_out3), .out4(demultiplexer_1_out4), .out5(demultiplexer_1_out5),
    .out6(demultiplexer_1_out6), .out7(demultiplexer_1_out7), .in(WE), .sel(REG_inSel));
  Register #(.width(32)) reg0 (.D(inData), .en(demultiplexer_1_out0), .clk(CLK), .Q(reg0_q));  // open: clr
  Register #(.width(32)) reg1 (.D(inData), .en(demultiplexer_1_out1), .clk(CLK), .Q(reg1_q));  // open: clr
  Register #(.width(32)) reg2 (.D(inData), .en(demultiplexer_1_out2), .clk(CLK), .Q(reg2_q));  // open: clr
  Register #(.width(32)) reg3 (.D(inData), .en(demultiplexer_1_out3), .clk(CLK), .Q(reg3_q));  // open: clr
  Register #(.width(32)) reg4 (.D(inData), .en(demultiplexer_1_out4), .clk(CLK), .Q(reg4_q));  // open: clr
  Register #(.width(32)) reg5 (.D(inData), .en(demultiplexer_1_out5), .clk(CLK), .Q(reg5_q));  // open: clr
  Register #(.width(32)) reg6 (.D(inData), .en(demultiplexer_1_out6), .clk(CLK), .Q(reg6_q));  // open: clr
  Register #(.width(32)) reg7 (.D(inData), .en(demultiplexer_1_out7), .clk(CLK), .Q(reg7_q));  // open: clr
  Multiplexer #(.enable("true"), .select(3), .width(32)) multiplexer_1 (
    .in0(reg0_q), .in1(reg1_q), .in2(reg2_q), .in3(reg3_q), .in4(reg4_q), .in5(reg5_q), .in6(reg6_q),
    .in7(reg7_q), .out(regOut), .sel(REG_outSel), .en(OUT_enb));
endmodule

module ControlUnit (
  input  CLK,
  input  [31:0] IR_in,
  output [19:0] controlBits
);

  wire decoder_1_out4, undriven, undriven_2, undriven_3, undriven_4;
  wire [1:0] and_1_out;
  wire [2:0] controlled_buffer_1_out, controlled_buffer_2_out, postaA_q, postaB_q;
  wire [3:0] counter_1_q;
  wire [7:0] counter_2_q, rom_1_data;

  ROM rom_1 (.addr(IR_in[31:24]), .data(rom_1_data));
  Register #(.width(3)) postaA (.D(IR_in[20:18]), .en(undriven_2), .clk(CLK), .Q(postaA_q));  // open: clr
  Register #(.width(3)) postaB (.D(IR_in[23:21]), .en(undriven), .clk(CLK), .Q(postaB_q));  // open: clr
  Decoder #(.enable("false"), .select(4)) decoder_1 (
    .out4(decoder_1_out4), .sel(counter_1_q));  // open: out0, out1, out2, out3, out5, out6, out7, out8, out9, out10, out11, out12, out13, out14, out15
  Counter #(.max('hf), .width(4)) counter_1 (
    .Q(counter_1_q), .clk(CLK), .clr(and_1_out[0]));  // open: load, D, count, carry, up
  assign controlled_buffer_1_out = undriven_3 ? postaA_q : 3'bz;  // Controlled_Buffer controlled_buffer_1
  Counter counter_2 (
    .load(decoder_1_out4), .D(rom_1_data), .Q(counter_2_q), .clk(CLK), .clr(and_1_out[0]));  // open: count, carry, up
  assign controlled_buffer_2_out = undriven_4 ? postaB_q : 3'bz;  // Controlled_Buffer controlled_buffer_2
  ROM #(.dataWidth(20)) rom_2 (.addr(counter_2_q), .data(controlBits));
  assign and_1_out = controlBits[19:18] & controlBits[17:16] & controlBits[15:14] & controlBits[13:12] & controlBits[11:10] & controlBits[9:8] & controlBits[7:6] & controlBits[5:4] & controlBits[3:2] & controlBits[1:0];  // AND_Gate and_1, 2 bits wide

  // Notes on the sheet:
  //   contents of rom_2 (hex, n*v repeats v):
  //   10004 11 60 fffff
endmodule
