// Logisim project t1_keyboardInput.circ as structural Verilog: 1 circuit, main circuit main
module main (
  input  adr_bus
);

  wire and_1_out, clock_1_out, decoder_1_out0, decoder_1_out1, Interrupt_q, keyboard_1_avail;
  wire [2:0] controlled_buffer_1_out;
  wire [3:0] controlled_buffer_1_out_2;
  wire [6:0] keyboard_1_data;

  Decoder #(.enable("false")) decoder_1 (.out0(decoder_1_out0), .out1(decoder_1_out1), .sel(adr_bus));
  Clock clock_1 (.out(clock_1_out));
  and and_1 (and_1_out, clock_1_out, Interrupt_q);
  Keyboard keyboard_1 (.clk(and_1_out), .re(1'b1), .avail(keyboard_1_avail), .data(keyboard_1_data));  // open: clr
  assign {controlled_buffer_1_out_2, controlled_buffer_1_out} = decoder_1_out0 ? keyboard_1_data : 7'bz;  // Controlled_Buffer controlled_buffer_1
  Register #(.width(1)) Interrupt (.D(keyboard_1_avail), .en(1'b1), .clk(clock_1_out), .Q(Interrupt_q));  // open: clr
  Hex_Digit_Display hex_digit_display_1 (.value(controlled_buffer_1_out_2));  // open: dp
  Hex_Digit_Display hex_digit_display_2 (.value({1'b0, controlled_buffer_1_out}));  // open: dp

  // Notes on the sheet:
  //   MemoryMap I/O Decoder
  //   DataBus
  //   CPU
endmodule
